// Logisim project mips_processor.circ as structural Verilog
module IMEM (
);

  wire [31:0] adder_1_out, PC_q;

  Register #(.width(32)) PC (.D(adder_1_out), .Q(PC_q));  // open: en, clk, clr
  Adder #(.width(32)) adder_1 (.a(32'h4), .b(PC_q), .out(adder_1_out));  // open: cin, cout
  RAM #(.addrWidth(24), .dataWidth(32)) ram_1 (.addr(PC_q[23:0]));  // open: data, sel, clk, ld, clr
endmodule

module REGFILE (
  input  RegWrite,
  input  [4:0] RegWrite_2,
  output [31:0] ReadData1,
  output [31:0] ReadData2
);

  wire clk, decoder_1_out0, decoder_1_out1, decoder_1_out2, decoder_1_out3, decoder_1_out4, decoder_1_out5,
       decoder_1_out6, decoder_1_out7, decoder_1_out8, decoder_1_out9, decoder_1_out10, decoder_1_out11,
       decoder_1_out12, decoder_1_out13, decoder_1_out14, decoder_1_out15, decoder_1_out16, decoder_1_out17,
       decoder_1_out18, decoder_1_out19, decoder_1_out20, decoder_1_out21, decoder_1_out22, decoder_1_out23,
       decoder_1_out24, decoder_1_out25, decoder_1_out26, decoder_1_out27, decoder_1_out28, decoder_1_out29,
       decoder_1_out30, decoder_1_out31;
  wire [4:0] readRegister1_2_q, readRegister1_q;
  wire [31:0] a0, a1, a2, a3, at, fp, gp, k0, k1, ra, s0, s1, s2, s3, s4, s5, s6, s7, sp, t0, t1, t2, t3, t4,
       t5, t6, t7, t8, t9, v0, v1, Wa0, Wa1, Wa2, Wa3, Wat, Wgp, Wk0, Wk1, Wra, Ws0, Ws1, Ws2, Ws3, Ws4, Ws5,
       Ws6, Ws7, Wsp, Wt0, Wt1, Wt2, Wt3, Wt4, Wt5, Wt6, Wt7, Wt8, Wt9, Wv0, Wv1, WZero, Zero;

  Register #(.width(5)) readRegister1 (.Q(readRegister1_q));  // open: D, en, clk, clr
  Decoder #(.select(5)) decoder_1 (
    .out0(decoder_1_out0), .out1(decoder_1_out1), .out2(decoder_1_out2), .out3(decoder_1_out3),
    .out4(decoder_1_out4), .out5(decoder_1_out5), .out6(decoder_1_out6), .out7(decoder_1_out7),
    .out8(decoder_1_out8), .out9(decoder_1_out9), .out10(decoder_1_out10), .out11(decoder_1_out11),
    .out12(decoder_1_out12), .out13(decoder_1_out13), .out14(decoder_1_out14), .out15(decoder_1_out15),
    .out16(decoder_1_out16), .out17(decoder_1_out17), .out18(decoder_1_out18), .out19(decoder_1_out19),
    .out20(decoder_1_out20), .out21(decoder_1_out21), .out22(decoder_1_out22), .out23(decoder_1_out23),
    .out24(decoder_1_out24), .out25(decoder_1_out25), .out26(decoder_1_out26), .out27(decoder_1_out27),
    .out28(decoder_1_out28), .out29(decoder_1_out29), .out30(decoder_1_out30), .out31(decoder_1_out31),
    .sel(RegWrite_2), .en(RegWrite));
  Register #(.width(5)) readRegister1_2 (.Q(readRegister1_2_q));  // open: D, en, clk, clr
  Multiplexer #(.select(5), .width(32), .enable("false")) multiplexer_1 (
    .in0(Zero), .in1(at), .in2(v0), .in3(v1), .in4(a0), .in5(a1), .in6(a2), .in7(a3), .in8(t0), .in9(t1),
    .in10(t2), .in11(t3), .in12(t4), .in13(t5), .in14(t6), .in15(t7), .in16(s0), .in17(s1), .in18(s2),
    .in19(s3), .in20(s4), .in21(s5), .in22(s6), .in23(s7), .in24(t8), .in25(t9), .in26(k0), .in27(k1),
    .in28(gp), .in29(sp), .in30(fp), .in31(ra), .out(ReadData1), .sel(readRegister1_q));
  Multiplexer #(.select(5), .width(32), .enable("false")) multiplexer_2 (
    .in0(Zero), .in1(ra), .in2(at), .in3(v0), .in4(v1), .in5(a0), .in6(a1), .in7(a2), .in8(a3), .in9(t0),
    .in10(t1), .in11(t2), .in12(t3), .in13(t4), .in14(t5), .in15(t6), .in16(t7), .in17(s0), .in18(s1),
    .in19(s2), .in20(s3), .in21(s4), .in22(s5), .in23(s6), .in24(s7), .in25(t8), .in26(t9), .in27(gp),
    .in28(sp), .in29(k0), .in30(k1), .in31(fp), .out(ReadData2), .sel(readRegister1_2_q));
  Register #(.width(32)) writedata ();  // open: D, en, Q, clk, clr
  Clock clock_1 (.out(clk));
  Register #(.width(32)) read_data1 (.D(Wv0), .Q(v0));  // open: en, clk, clr
  Register #(.width(32)) read_data1_2 (.D(Wv1), .Q(v1));  // open: en, clk, clr
  Register #(.width(32)) read_data1_3 (.D(WZero), .Q(Zero));  // open: en, clk, clr
  Register #(.width(32)) read_data1_4 (.D(Wa0), .Q(a0));  // open: en, clk, clr
  Register #(.width(32)) read_data1_5 (.D(Wa1), .Q(a1));  // open: en, clk, clr
  Register #(.width(32)) read_data1_6 (.D(Wa2), .Q(a2));  // open: en, clk, clr
  Register #(.width(32)) read_data1_7 (.D(Wa3), .Q(a3));  // open: en, clk, clr
  Register #(.width(32)) read_data1_8 (.D(Wt0), .Q(t0));  // open: en, clk, clr
  Register #(.width(32)) read_data1_9 (.D(Wt1), .Q(t1));  // open: en, clk, clr
  Register #(.width(32)) read_data1_10 (.D(Wt2), .Q(t2));  // open: en, clk, clr
  Register #(.width(32)) read_data1_11 (.D(Wt8), .Q(t8));  // open: en, clk, clr
  Register #(.width(32)) read_data1_12 (.D(Wt9), .Q(t9));  // open: en, clk, clr
  Register #(.width(32)) read_data1_13 (.D(Wk0), .Q(k0));  // open: en, clk, clr
  Register #(.width(32)) read_data1_14 (.D(Wk1), .Q(k1));  // open: en, clk, clr
  Register #(.width(32)) read_data1_15 (.D(Wgp), .Q(gp));  // open: en, clk, clr
  Register #(.width(32)) read_data1_16 (.D(Wk1), .Q(fp));  // open: en, clk, clr
  Register #(.width(32)) read_data1_17 (.D(Wat), .Q(at));  // open: en, clk, clr
  Register #(.width(32)) read_data1_18 (.D(Ws0), .Q(s0));  // open: en, clk, clr
  Register #(.width(32)) read_data1_19 (.D(Ws1), .Q(s1));  // open: en, clk, clr
  Register #(.width(32)) read_data1_20 (.D(Ws2), .Q(s2));  // open: en, clk, clr
  Register #(.width(32)) read_data1_21 (.D(Wt7), .Q(t7));  // open: en, clk, clr
  Register #(.width(32)) read_data1_22 (.D(Wt6), .Q(t6));  // open: en, clk, clr
  Register #(.width(32)) read_data1_23 (.D(Wt5), .Q(t5));  // open: en, clk, clr
  Register #(.width(32)) read_data1_24 (.D(Wt4), .Q(t4));  // open: en, clk, clr
  Register #(.width(32)) read_data1_25 (.D(Wt3), .Q(t3));  // open: en, clk, clr
  Register #(.width(32)) read_data1_26 (.D(Ws3), .Q(s3));  // open: en, clk, clr
  Register #(.width(32)) read_data1_27 (.D(Ws4), .Q(s4));  // open: en, clk, clr
  Register #(.width(32)) read_data1_28 (.D(Ws5), .Q(s5));  // open: en, clk, clr
  Register #(.width(32)) read_data1_29 (.D(Ws6), .Q(s6));  // open: en, clk, clr
  Register #(.width(32)) read_data1_30 (.D(Ws7), .Q(s7));  // open: en, clk, clr
  Register #(.width(32)) read_data1_31 (.D(Wsp), .Q(sp));  // open: en, clk, clr
  Register #(.width(32)) read_data1_32 (.D(Wra), .Q(ra));  // open: en, clk, clr
endmodule

module IF_ID (
  input  CLEAR,
  input  [31:0] INSTRUCTION,
  input  [31:0] PC,
  input  ENABLE,
  input  CLK,
  output [5:0] OPCODE,
  output [4:0] RS,
  output [4:0] RT,
  output [4:0] RD,
  output [4:0] SHAMT,
  output [5:0] FUNCT,
  output [15:0] IMMEDIATE,
  output [25:0] ADDRESS,
  output [31:0] PC_2
);

  wire not_1_out;

  Register #(.width(32)) u_instruction (
    .D(INSTRUCTION), .en(ENABLE), .Q({OPCODE, ADDRESS}), .clk(not_1_out), .clr(CLEAR));
  Register #(.width(32)) program_counter (.D(PC), .en(ENABLE), .Q(PC_2), .clk(not_1_out), .clr(CLEAR));
  not not_1 (not_1_out, CLK);
  S_R_Flip_Flop s_r_ff_1 ();  // open: S, clk, R, Q, Qn, preset, reset, en

  assign FUNCT = ADDRESS[5:0];
  assign IMMEDIATE = ADDRESS[15:0];
  assign RD = ADDRESS[15:11];
  assign RS = ADDRESS[25:21];
  assign RT = ADDRESS[20:16];
  assign SHAMT = ADDRESS[10:6];
endmodule

module ID_EX (
  input  CLEAR,
  input  [31:0] PC,
  input  RegWrite,
  input  MemToReg,
  input  MemWrite,
  input  MemRead,
  input  Branch,
  input  [1:0] AluOp,
  input  RegDst,
  input  AluSrc,
  input  [31:0] ReadData1,
  input  [31:0] ReadData2,
  input  [31:0] Immediate,
  input  [4:0] RT,
  input  [4:0] RD,
  input  ENABLE,
  input  CLK,
  output [31:0] PC_2,
  output RegWrite_2,
  output MemToReg_2,
  output MemWrite_2,
  output MemRead_2,
  output Branch_2,
  output [1:0] AluOp_2,
  output RegDst_2,
  output AluSrc_2,
  output [31:0] ReadData1_2,
  output [31:0] ReadData2_2,
  output [31:0] IMMEADIATE,
  output [4:0] RT_2,
  output [4:0] RD_2
);

  wire not_1_out;

  not not_1 (not_1_out, CLK);
  Register #(.width(32)) program_counter (.D(PC), .en(ENABLE), .Q(PC_2), .clk(not_1_out), .clr(CLEAR));
  Register #(.width(2)) wb (
    .D({RegWrite, MemToReg}), .en(ENABLE), .Q({RegWrite_2, MemToReg_2}), .clk(not_1_out), .clr(CLEAR));
  Register #(.width(3)) mem (
    .D({MemWrite, MemRead, Branch}), .en(ENABLE), .Q({MemWrite_2, MemRead_2, Branch_2}), .clk(not_1_out),
    .clr(CLEAR));
  Register #(.width(4)) ex (
    .D({AluOp, RegDst, AluSrc}), .en(ENABLE), .Q({AluOp_2, RegDst_2, AluSrc_2}), .clk(not_1_out), .clr(CLEAR));
  Register #(.width(32)) read_data1 (.D(ReadData1), .en(ENABLE), .Q(ReadData1_2), .clk(not_1_out), .clr(CLEAR));
  Register #(.width(32)) read_data2 (.D(ReadData2), .en(ENABLE), .Q(ReadData2_2), .clk(not_1_out), .clr(CLEAR));
  Register #(.width(32)) u_immediate (.D(Immediate), .en(ENABLE), .Q(IMMEADIATE), .clk(not_1_out), .clr(CLEAR));
  Register #(.width(5)) u_rt (.D(RT), .en(ENABLE), .Q(RT_2), .clk(not_1_out), .clr(CLEAR));
  Register #(.width(5)) u_rd (.D(RD), .en(ENABLE), .Q(RD_2), .clk(not_1_out), .clr(CLEAR));
endmodule
